# Fritzing sketch brazaletePOV (saved by Fritzing 0.8.7b)

parts:
  Part1 = LilyPad Arduino Simple Board
  Part2 = LilyPad LED
  Part3 = LilyPad LED
  Part4 = LilyPad LED
  Part5 = LilyPad LED
  Part6 = LilyPad LED

nets:
  N1: Part1.GND, Part2.-, Part3.-, Part4.-, Part5.-, Part6.-
